# Fritzing sketch Schematic and PCB (saved by Fritzing 0.9.3b)
circuit board: 8.46667cm x 5.64444cm
breadboards: 1

parts:
  U1 = Voltage Regulator [package=to220-adj]
  D1 = Rectifier Diode [part_number=1N4001 package="300 mil [THT]"]
  C1 = Electrolytic Capacitor [capacitance=1µF package="100 mil [THT, electrolytic]"]
  C2 = Electrolytic Capacitor [capacitance=1µF package="100 mil [THT, electrolytic]"]
  R1 = Resistor [tolerance=±5% resistance=220 package=THT]
  R2 = Resistor [tolerance=±5% resistance=220 package=THT]
  R3 = Resistor [tolerance=±5% resistance=220 package=THT]
  LED1 = LED - 5mm [color="Red (633nm)" package="5 mm [THT]"]
  LED2 = LED - 5mm [color="Red (633nm)" package="5 mm [THT]"]
  XTAL1 = Crystal [frequency="16 Mhz" package=THT]
  J2 = female pin header, 6 pins [form="♀ (female)"]
  J3 = female pin header, 6 pins [form="♀ (female)"]
  IC1 = IC, DIP package, 28 pins [chip_label=IC]
  J4 = female pin header, 4 pins [form="♀ (female)"]
  J5 = female pin header, 8 pins [form="♀ (female)"]
  C3 = Ceramic Capacitor [capacitance=100nF package="100 mil [THT, multilayer]"]
  C4 = Ceramic Capacitor [capacitance=100nF package="100 mil [THT, multilayer]"]
  S1 = Toggle Switch [package=THT]
  S2 = Pushbutton [package="[THT]"]
  C5 = Capacitor [package=cap-pth-small]
  Power_plug1 = Power plug

nets (from the schematic view):
  N1: U1.ADJ, C1.-, C2.-, LED2.cathode, IC1.pin1, S2.Pin_1, S2.Pin_2, C5.1, Power_plug1.GND
  N2: U1.IN, C1.+, S1.L1
  N3: U1.OUT, C2.+, R1.Pin_0, R2.Pin_1, J3.pin1, IC1.pin7, IC1.pin20, IC1.pin21, J5.pin7
  N4: D1.cathode, S1.COM
  N5: D1.anode, Power_plug1.VCC
  N6: R1.Pin_1, S2.Pin_3, S2.Pin_4
  N7: R2.Pin_0, LED2.anode
  N8: R3.Pin_0, J3.pin2, IC1.pin19
  N9: R3.Pin_1, LED1.anode
  N10: LED1.cathode, IC1.pin8, IC1.pin22, J5.pin8, C3.0, C4.0
  N11: XTAL1.pin_0, IC1.pin9, C3.1
  N12: XTAL1.pin_1, IC1.pin10, C4.1
  N13: J2.pin1, IC1.pin28
  N14: J2.pin2, IC1.pin27
  N15: J2.pin3, IC1.pin26
  N16: J2.pin4, IC1.pin25
  N17: J2.pin5, IC1.pin24
  N18: J2.pin6, IC1.pin23
  N19: J3.pin3, IC1.pin18
  N20: J3.pin4, IC1.pin17
  N21: J3.pin5, IC1.pin16
  N22: J3.pin6, IC1.pin15
  N23: IC1.pin2, J5.pin2
  N24: IC1.pin3, J5.pin3
  N25: IC1.pin4, J5.pin4
  N26: IC1.pin5, J5.pin5
  N27: IC1.pin6, J5.pin6
  N28: IC1.pin11, J4.pin1
  N29: IC1.pin12, J4.pin2
  N30: IC1.pin13, J4.pin3
  N31: IC1.pin14, J4.pin4
  N32: J5.pin1, C5.2
