# Fritzing sketch project 4 breadboard (saved by Fritzing 0.9.3b)
circuit board: 8.46667cm x 5.64444cm
breadboards: 1

parts:
  Power_plug1 = Power plug
  D1 = Rectifier Diode [part_number=1N4001 package="300 mil [THT]"]
  S1 = Toggle Switch [package=THT]
  U1 = Voltage Regulator - 5V [package="TO220 [THT]"]
  C1 = Electrolytic Capacitor [capacitance=1µF package="100 mil [THT, electrolytic]"]
  C2 = Electrolytic Capacitor [capacitance=1µF package="100 mil [THT, electrolytic]"]
  R1 = Resistor [tolerance=±5% resistance=220 package=THT]
  LED1 = LED - 5mm [color="Red (633nm)" package="5 mm [THT]"]
  S2 = Pushbutton [package="[THT]"]
  U2 = atmega328 [package=dip]
  R2 = Resistor [tolerance=±5% resistance=220 package=THT]
  LED2 = LED - 5mm [color="Red (633nm)" package="5 mm [THT]"]
  XTAL1 = Crystal [frequency="16 Mhz" package=THT]
  R3 = Resistor [tolerance=±5% resistance=220 package=THT]
  C3 = Ceramic Capacitor [capacitance=100nF package="100 mil [THT, multilayer]"]
  C4 = Ceramic Capacitor [capacitance=100nF package="100 mil [THT, multilayer]"]
  C5 = Capacitor [package=cap-pth-small2]

nets:
  GND: Power_plug1.GND, U1.GND, C1.-, C2.-, LED1.cathode, S2.Pin_3, S2.Pin_4, U2.GND, LED2.cathode, C3.1, C4.1
  VCC: Power_plug1.VCC, D1.cathode, U2.VCC, R3.Pin_1
  N1: D1.anode, S1.COM
  N2: S1.L2, U1.input_voltage, C1.+
  N3: U1.output_voltage, C2.+, R1.Pin_0
  N4: R1.Pin_1, LED1.anode, U2.AVCC, U2.AREF
  N5: S2.Pin_1, S2.Pin_2, U2.RESET, R3.Pin_0, C5.1
  N6: U2.XLAT1, XTAL1.pin_0, C4.0
  N7: U2.XLAT2, XTAL1.pin_1, C3.0
  N8: U2.D13, R2.Pin_0
  N9: R2.Pin_1, LED2.anode
